// Logisim project sagui.circ as structural Verilog: 7 circuits, main circuit main
module main (
);

  wire and_1_out, and_2_out, and_3_out, Branch, CLK, IMM_Control, Jump, MOV_Control, MR, or_1_out, or_2_out,
       PC_Src, Reg_D, Reg_Src, Reg_W, Reset, WE, ZERO;
  wire [1:0] Ra, Rb, Rd;
  wire [2:0] ALU_Control;
  wire [3:0] OPCode;
  wire [7:0] adder_1_out, adder_2_out, Data, IMM, multiplexer_1_out, multiplexer_2_out, multiplexer_4_out,
       multiplexer_5_out, PC_q, ram_1_dout, S1, S2, ula_1_s;

  Multiplexer #(.width(8)) multiplexer_1 (.in0(multiplexer_2_out), .in1(S2), .out(multiplexer_1_out), .sel(and_1_out));
  and and_1 (and_1_out, or_1_out, PC_Src);
  or or_1 (or_1_out, Jump, and_2_out);
  Register PC (.D(multiplexer_1_out), .en(1'b1), .clk(CLK), .Q(PC_q), .clr(Reset));
  and and_2 (and_2_out, ZERO, Branch);
  Button u_Reset (.out(Reset));
  Clock u_CLK (.out(CLK));
  Adder adder_1 (.a(8'h1), .b(PC_q), .out(adder_1_out));  // open: cin, cout
  ROM InstructionMemory (.addr(PC_q), .data({OPCode, Ra, Rb}));
  Adder adder_2 (.a(PC_q), .b(IMM), .out(adder_2_out));  // open: cin, cout
  Multiplexer #(.width(8)) multiplexer_2 (
    .in0(adder_1_out), .in1(adder_2_out), .out(multiplexer_2_out), .sel(or_2_out));
  or or_2 (or_2_out, and_3_out, Jump);
  and and_3 (and_3_out, ZERO, Branch);
  Multiplexer #(.width(2)) multiplexer_3 (.in0(Ra), .in1(2'b00), .out(Rd), .sel(Reg_D));
  Multiplexer #(.width(8)) multiplexer_4 (.in0(Data), .in1(S2), .out(multiplexer_4_out), .sel(MR));
  Control_Center control_center_1 (
    .OPCode(OPCode), .Branch(Branch), .Jump(Jump), .PC_Src(PC_Src), .Reg_D(Reg_D), .MR(MR), .Reg_W(Reg_W),
    .IMM_Control(IMM_Control), .ALU_Control(ALU_Control), .MOV_Control(MOV_Control), .WE(WE),
    .Reg_Src(Reg_Src));
  BancoDeRegistrador bancoderegistrador_1 (
    .Ra(Rd), .Rb(Rb), .CLK(CLK), .WD(multiplexer_4_out), .WriteReg(Rd), .WE(Reg_W), .R(Reset), .Rd1(S1),
    .Rd2(S2));
  Extend extend_1 (.IMM({OPCode, Ra, Rb}), .S(IMM));
  Multiplexer #(.width(8)) multiplexer_5 (.in0(S2), .in1(IMM), .out(multiplexer_5_out), .sel(IMM_Control));
  ULA ula_1 (
    .A(S1), .B(multiplexer_5_out), .ALU_Control(ALU_Control), .MOV_Control(MOV_Control), .ZERO(ZERO),
    .S(ula_1_s));
  RAM #(.asyncread("true")) ram_1 (.addr(S2), .we(WE), .oe(1'b1), .clk(CLK), .din(S1), .dout(ram_1_dout));
  Multiplexer #(.width(8)) multiplexer_6 (.in0(ram_1_dout), .in1(ula_1_s), .out(Data), .sel(Reg_Src));

  // Notes on the sheet:
  //   contents of InstructionMemory (hex, n*v repeats v):
  //   81 6c a0 89 64 a0 8a 68 9b 5a 9b 54 a3 12 21 a0 a5 ab 8a 64 4c 91 48 9e a1 5c 6c a0 81 ac 63 69 99
  //   12 22 30
endmodule

module SLR (
  input  [7:0] A,
  input  [7:0] B,
  output [7:0] S
);

  wire or_1_out;
  wire [7:0] shifter_1_out;

  Shifter shifter_1 (.in(A), .\dist (B[2:0]), .out(shifter_1_out));
  or or_1 (or_1_out, B[3], B[4], B[5], B[6], B[7]);
  Multiplexer #(.width(8)) multiplexer_1 (.in0(shifter_1_out), .in1({8{1'b0}}), .out(S), .sel(or_1_out));
endmodule

module ULA (
  input  [7:0] A,
  input  [7:0] B,
  input  [2:0] ALU_Control,
  input  MOV_Control,
  output ZERO,
  output [7:0] S
);

  wire [7:0] adder_1_out, and_1_out, multiplexer_1_out, not_1_out, not_2_out, or_1_out, slr_1_s, srr_1_s,
       subtractor_1_out;

  assign not_1_out = ~B;  // NOT_Gate not_1, 8 bits wide
  Adder adder_1 (.a(A), .b(B), .out(adder_1_out));  // open: cin, cout
  Subtractor subtractor_1 (.a(A), .b(B), .out(subtractor_1_out));  // open: bin, bout
  assign and_1_out = A & B;  // AND_Gate and_1, 8 bits wide
  assign or_1_out = A | B;  // OR_Gate or_1, 8 bits wide
  assign not_2_out = ~A;  // NOT_Gate not_2, 8 bits wide
  SLR slr_1 (.A(A), .B(B), .S(slr_1_s));
  SRR srr_1 (.A(A), .B(B), .S(srr_1_s));
  Multiplexer #(.width(8)) multiplexer_1 (
    .in0({A[7:4], B[3:0]}), .in1({B[3:0], A[3:0]}), .out(multiplexer_1_out), .sel(MOV_Control));
  Multiplexer #(.select(3), .width(8)) multiplexer_2 (
    .in0(adder_1_out), .in1(subtractor_1_out), .in2(and_1_out), .in3(or_1_out), .in4(not_1_out),
    .in5(slr_1_s), .in6(srr_1_s), .in7(multiplexer_1_out), .out(S), .sel(ALU_Control));
  and and_2 (ZERO, not_2_out[0], not_2_out[1], not_2_out[2], not_2_out[3], not_2_out[4], not_2_out[5], not_2_out[6], not_2_out[7]);

  // Other names for the same wires on the sheet: Bits[3:0] = B[3:0]
endmodule

module SRR (
  input  [7:0] A,
  input  [7:0] B,
  output [7:0] S
);

  wire or_1_out;
  wire [7:0] shifter_1_out;

  Shifter #(.shift("lr")) shifter_1 (.in(A), .\dist (B[2:0]), .out(shifter_1_out));
  or or_1 (or_1_out, B[3], B[4], B[5], B[6], B[7]);
  Multiplexer #(.width(8)) multiplexer_1 (.in0(shifter_1_out), .in1({8{1'b0}}), .out(S), .sel(or_1_out));
endmodule

module BancoDeRegistrador (
  input  [1:0] Ra,
  input  [1:0] Rb,
  input  CLK,
  input  [7:0] WD,
  input  [1:0] WriteReg,
  input  WE,
  input  R,
  output [7:0] Rd1,
  output [7:0] Rd2
);

  wire W0, W1, W2, W3;
  wire [7:0] demultiplexer_1_out0, demultiplexer_1_out1, demultiplexer_1_out2, demultiplexer_1_out3, R0, R1,
       R2, R3;

  Demultiplexer #(.select(2), .width(8)) demultiplexer_1 (
    .out0(demultiplexer_1_out0), .out1(demultiplexer_1_out1), .out2(demultiplexer_1_out2),
    .out3(demultiplexer_1_out3), .in(WD), .sel(WriteReg));
  Demultiplexer #(.select(2)) demultiplexer_2 (.out0(W0), .out1(W1), .out2(W2), .out3(W3), .in(WE), .sel(WriteReg));
  Register register_1 (.D(demultiplexer_1_out0), .en(W0), .clk(CLK), .Q(R0), .clr(R));
  Register register_2 (.D(demultiplexer_1_out1), .en(W1), .clk(CLK), .Q(R1), .clr(R));
  Register register_3 (.D(demultiplexer_1_out2), .en(W2), .clk(CLK), .Q(R2), .clr(R));
  Register register_4 (.D(demultiplexer_1_out3), .en(W3), .clk(CLK), .Q(R3), .clr(R));
  Multiplexer #(.select(2), .width(8)) multiplexer_1 (.in0(R0), .in1(R1), .in2(R2), .in3(R3), .out(Rd1), .sel(Ra));
  Multiplexer #(.select(2), .width(8)) multiplexer_2 (.in0(R0), .in1(R1), .in2(R2), .in3(R3), .out(Rd2), .sel(Rb));
endmodule

module Extend (
  input  [7:0] IMM,
  output [7:0] S
);

  assign S = {{4{IMM[3]}}, IMM[3:0]};  // Bit_Extender bit_extender_1
endmodule

module Control_Center (
  input  [3:0] OPCode,
  output Branch,
  output Jump,
  output PC_Src,
  output Reg_D,
  output MR,
  output Reg_W,
  output IMM_Control,
  output [2:0] ALU_Control,
  output MOV_Control,
  output WE,
  output Reg_Src
);

  ROM #(.addrWidth(4), .dataWidth(13)) rom_1 (
    .addr(OPCode),
    .data({Branch, Jump, PC_Src, Reg_D, MR, Reg_W, IMM_Control, ALU_Control, MOV_Control, WE, Reg_Src}));

  // Notes on the sheet:
  //   contents of rom_1 (hex, n*v repeats v):
  //   1400 1200 c00 800 80 2 180 2fd 2f9 81 89 91 99 a1 a9 b1
endmodule
