// Logisim project sagui.circ as structural Verilog: 10 circuits, main circuit main
module main (
);

  wire and_1_out, Branch, CLK, Reset, S_Reg_D, S_RWE, S_WE, V_Reg_D, V_RWE, V_WE, ZERO;
  wire [1:0] Reg_Src_Scalar, Reg_Src_Vector, S_ALU_Control, S_Ra, S_Rb, S_Rd, V_ALU_Control, V_Ra, V_Rb, V_Rd;
  wire [3:0] IMM, Opcode;
  wire [7:0] adder_1_out, multiplexer_1_out, PC_q, ram_1_dout, ram_2_dout, ram_3_dout, ram_4_dout,
       ram_5_dout, rom_1_data, S_Data, S_MOVH, S_MOVL, S_Rd1, S_Rd2, S_S, V0_Data, V0_MOVH, V0_MOVL, V0_Rd1,
       V0_Rd2, V0_S, V1_Data, V1_MOVH, V1_MOVL, V1_Rd1, V1_Rd2, V1_S, V2_Data, V2_MOVH, V2_MOVL, V2_Rd1,
       V2_Rd2, V2_S, V3_Data, V3_MOVH, V3_MOVL, V3_Rd1, V3_Rd2, V3_S;

  Multiplexer #(.width(8)) multiplexer_1 (.in0(adder_1_out), .in1(S_Rd2), .out(multiplexer_1_out), .sel(and_1_out));
  and and_1 (and_1_out, Branch, ZERO);
  Register PC (.D(multiplexer_1_out), .en(1'b1), .clk(CLK), .Q(PC_q), .clr(Reset));
  Clock clock_1 (.out(CLK));
  Button button_1 (.out(Reset));
  Controle Control_Center (
    .Opcode(Opcode), .Reg_Src_Vector(Reg_Src_Vector), .V_RWE(V_RWE), .V_WE(V_WE),
    .V_ALU_Control(V_ALU_Control), .V_Reg_D(V_Reg_D), .Branch(Branch), .Reg_Src_Scalar(Reg_Src_Scalar),
    .S_RWE(S_RWE), .S_WE(S_WE), .S_ALU_Control(S_ALU_Control), .S_Reg_D(S_Reg_D));
  Adder adder_1 (.a(8'h1), .b(PC_q), .out(adder_1_out));  // open: cin, cout
  ROM rom_1 (.addr(PC_q), .data(rom_1_data));
  Inst_Decoder Decode (
    .Data(rom_1_data), .V_Ra(V_Ra), .V_Rb(V_Rb), .S_Ra(S_Ra), .S_Rb(S_Rb), .IMM(IMM), .Opcode(Opcode));
  MOV_L MOVL_V0 (.R1(V0_Rd1), .IMM(IMM), .S(V0_MOVL));
  MOV_H MOVH_V0 (.R1(V0_Rd1), .IMM(IMM), .S(V0_MOVH));
  MOV_L MOVL_V1 (.R1(V1_Rd1), .IMM(IMM), .S(V1_MOVL));
  MOV_H MOVH_V1 (.R1(V1_Rd1), .IMM(IMM), .S(V1_MOVH));
  MOV_L MOVL_V2 (.R1(V2_Rd1), .IMM(IMM), .S(V2_MOVL));
  MOV_H MOVH_V2 (.R1(V2_Rd1), .IMM(IMM), .S(V2_MOVH));
  MOV_L MOVL_V3 (.R1(V3_Rd1), .IMM(IMM), .S(V3_MOVL));
  MOV_H MOVH_V3 (.R1(V3_Rd1), .IMM(IMM), .S(V3_MOVH));
  MOV_L MOVL_S (.R1(S_Rd1), .IMM(IMM), .S(S_MOVL));
  MOV_H MOVH_S (.R1(S_Rd1), .IMM(IMM), .S(S_MOVH));
  Multiplexer #(.width(2)) multiplexer_2 (.in0(V_Ra), .in1(2'b01), .out(V_Rd), .sel(V_Reg_D));
  Multiplexer #(.width(2)) multiplexer_3 (.in0(S_Ra), .in1(2'b01), .out(S_Rd), .sel(S_Reg_D));
  Scalar_BR VectorBR0 (
    .CLK(CLK), .WriteEnable(V_RWE), .Reset(Reset), .Ra(V_Rd), .Rb(V_Rb), .WriteRegister(V_Rd),
    .Data(V0_Data), .Rd1(V0_Rd1), .Rd2(V0_Rd2));
  Vector1BR VectorBR1 (
    .CLK(CLK), .WriteEnable(V_RWE), .Reset(Reset), .Ra(V_Rd), .Rb(V_Rb), .WriteRegister(V_Rd),
    .Data(V1_Data), .Rd1(V1_Rd1), .Rd2(V1_Rd2));
  Vector2BR VectorBR2 (
    .CLK(CLK), .WriteEnable(V_RWE), .Reset(Reset), .Ra(V_Rd), .Rb(V_Rb), .WriteRegister(V_Rd),
    .Data(V2_Data), .Rd1(V2_Rd1), .Rd2(V2_Rd2));
  Vector3BR VectorBR3 (
    .CLK(CLK), .WriteEnable(V_RWE), .Reset(Reset), .Ra(V_Rd), .Rb(V_Rb), .WriteRegister(V_Rd),
    .Data(V3_Data), .Rd1(V3_Rd1), .Rd2(V3_Rd2));
  Scalar_BR ScalarBR (
    .CLK(CLK), .WriteEnable(S_RWE), .Reset(Reset), .Ra(S_Rd), .Rb(S_Rb), .WriteRegister(S_Rd), .Data(S_Data),
    .Rd1(S_Rd1), .Rd2(S_Rd2));
  ULA VectorALU0 (.RA(V0_Rd1), .RB(V0_Rd2), .ALU_Control(V_ALU_Control), .S(V0_S));  // open: ZERO
  ULA VectorALU1 (.RA(V1_Rd1), .RB(V1_Rd2), .ALU_Control(V_ALU_Control), .S(V1_S));  // open: ZERO
  ULA VectorALU2 (.RA(V2_Rd1), .RB(V2_Rd2), .ALU_Control(V_ALU_Control), .S(V2_S));  // open: ZERO
  ULA VectorALU3 (.RA(V3_Rd1), .RB(V3_Rd2), .ALU_Control(V_ALU_Control), .S(V3_S));  // open: ZERO
  ULA ScalarALU (.RA(S_Rd1), .RB(S_Rd2), .ALU_Control(S_ALU_Control), .S(S_S), .ZERO(ZERO));
  RAM #(.asyncread("true")) ram_1 (.addr(V0_Rd2), .we(V_WE), .oe(1'b1), .clk(CLK), .din(V0_Rd1), .dout(ram_1_dout));
  RAM #(.asyncread("true")) ram_2 (.addr(V1_Rd2), .we(V_WE), .oe(1'b1), .clk(CLK), .din(V1_Rd1), .dout(ram_2_dout));
  RAM #(.asyncread("true")) ram_3 (.addr(V2_Rd2), .we(V_WE), .oe(1'b1), .clk(CLK), .din(V2_Rd1), .dout(ram_3_dout));
  RAM #(.asyncread("true")) ram_4 (.addr(V3_Rd2), .we(V_WE), .oe(1'b1), .clk(CLK), .din(V3_Rd1), .dout(ram_4_dout));
  RAM #(.asyncread("true")) ram_5 (.addr(S_Rd2), .we(S_WE), .oe(1'b1), .clk(CLK), .din(S_Rd1), .dout(ram_5_dout));
  Multiplexer #(.select(2), .width(8)) multiplexer_4 (
    .in0(ram_5_dout), .in1(S_S), .in2(S_MOVL), .in3(S_MOVH), .out(S_Data), .sel(Reg_Src_Scalar));
  Multiplexer #(.select(2), .width(8)) multiplexer_5 (
    .in0(ram_1_dout), .in1(V0_S), .in2(V0_MOVL), .in3(V0_MOVH), .out(V0_Data), .sel(Reg_Src_Vector));
  Multiplexer #(.select(2), .width(8)) multiplexer_6 (
    .in0(ram_2_dout), .in1(V1_S), .in2(V1_MOVL), .in3(V1_MOVH), .out(V1_Data), .sel(Reg_Src_Vector));
  Multiplexer #(.select(2), .width(8)) multiplexer_7 (
    .in0(ram_3_dout), .in1(V2_S), .in2(V2_MOVL), .in3(V2_MOVH), .out(V2_Data), .sel(Reg_Src_Vector));
  Multiplexer #(.select(2), .width(8)) multiplexer_8 (
    .in0(ram_4_dout), .in1(V3_S), .in2(V3_MOVL), .in3(V3_MOVH), .out(V3_Data), .sel(Reg_Src_Vector));

  // Notes on the sheet:
  //   Control
  //   contents of rom_1 (hex, n*v repeats v):
  //   31 21 14 55 31 4d 33 22 17 55 33 b4 a1 c9 d5 cc c8 b 9f bc cd 9b cd b0 97 bc dd dd b4 cd c9 57 76 8
  //   72 3b 49 18 32 21 49 1b 55 33 df cc b 8b bc cd 87 c9 d5 bc cd 9b dd dd b4 cd 57 76 8 72 72
  //   PC
  //   MOVS
  //   Register
  //   Vector
  //   Scalar
endmodule

module Scalar_BR (
  input  [1:0] Ra,
  input  [1:0] Rb,
  input  CLK,
  input  [7:0] Data,
  input  WriteEnable,
  input  [1:0] WriteRegister,
  input  Reset,
  output [7:0] Rd1,
  output [7:0] Rd2
);

  wire W1, W2, W3;
  wire [7:0] R0, R1, R2, R3;

  Demultiplexer #(.select(2)) demultiplexer_1 (
    .out1(W1), .out2(W2), .out3(W3), .in(WriteEnable), .sel(WriteRegister));  // open: out0
  Register u_R0 (.D({8{1'b0}}), .en(Reset), .clk(Reset), .Q(R0), .clr(1'b0));
  Register u_R1 (.D(Data), .en(W1), .clk(CLK), .Q(R1), .clr(Reset));
  Register u_R2 (.D(Data), .en(W2), .clk(CLK), .Q(R2), .clr(Reset));
  Register u_R3 (.D(Data), .en(W3), .clk(CLK), .Q(R3), .clr(Reset));
  Multiplexer #(.select(2), .width(8)) multiplexer_1 (.in0(R0), .in1(R1), .in2(R2), .in3(R3), .out(Rd1), .sel(Ra));
  Multiplexer #(.select(2), .width(8)) multiplexer_2 (.in0(R0), .in1(R1), .in2(R2), .in3(R3), .out(Rd2), .sel(Rb));
endmodule

module ULA (
  input  [7:0] RA,
  input  [7:0] RB,
  input  [1:0] ALU_Control,
  output ZERO,
  output [7:0] S
);

  wire [7:0] adder_1_out, and_1_out, not_1_out, or_1_out, subtractor_1_out;

  assign not_1_out = ~RA;  // NOT_Gate not_1, 8 bits wide
  Adder adder_1 (.a(RA), .b(RB), .out(adder_1_out));  // open: cin, cout
  Subtractor subtractor_1 (.a(RA), .b(RB), .out(subtractor_1_out));  // open: bin, bout
  assign and_1_out = RA & RB;  // AND_Gate and_1, 8 bits wide
  assign or_1_out = RA | RB;  // OR_Gate or_1, 8 bits wide
  and and_2 (ZERO, not_1_out[0], not_1_out[1], not_1_out[2], not_1_out[3], not_1_out[4], not_1_out[5], not_1_out[6], not_1_out[7]);
  Multiplexer #(.select(2), .width(8)) multiplexer_1 (
    .in0(adder_1_out), .in1(subtractor_1_out), .in2(and_1_out), .in3(or_1_out), .out(S), .sel(ALU_Control));
endmodule

module Inst_Decoder (
  input  [7:0] Data,
  output [1:0] V_Ra,
  output [1:0] V_Rb,
  output [1:0] S_Ra,
  output [1:0] S_Rb,
  output [3:0] IMM,
  output [3:0] Opcode
);

  Demultiplexer #(.width(4)) demultiplexer_1 (.out0({S_Ra, S_Rb}), .out1({V_Ra, V_Rb}), .in(Data[3:0]), .sel(Data[7]));

  assign IMM = Data[3:0];
  assign Opcode = Data[7:4];

  // Other names for the same wires on the sheet: Rb[1:0] = V_Rb; Ra[1:0] = V_Ra
endmodule

module Vector3BR (
  input  [1:0] Ra,
  input  [1:0] Rb,
  input  CLK,
  input  [7:0] Data,
  input  WriteEnable,
  input  [1:0] WriteRegister,
  input  Reset,
  output [7:0] Rd1,
  output [7:0] Rd2
);

  wire W1, W2, W3;
  wire [7:0] R0, R1, R2, R3;

  Demultiplexer #(.select(2)) demultiplexer_1 (
    .out1(W1), .out2(W2), .out3(W3), .in(WriteEnable), .sel(WriteRegister));  // open: out0
  Register u_R0 (.D(8'h3), .en(Reset), .clk(Reset), .Q(R0), .clr(1'b0));
  Register u_R1 (.D(Data), .en(W1), .clk(CLK), .Q(R1), .clr(Reset));
  Register u_R2 (.D(Data), .en(W2), .clk(CLK), .Q(R2), .clr(Reset));
  Register u_R3 (.D(Data), .en(W3), .clk(CLK), .Q(R3), .clr(Reset));
  Multiplexer #(.select(2), .width(8)) multiplexer_1 (.in0(R0), .in1(R1), .in2(R2), .in3(R3), .out(Rd1), .sel(Ra));
  Multiplexer #(.select(2), .width(8)) multiplexer_2 (.in0(R0), .in1(R1), .in2(R2), .in3(R3), .out(Rd2), .sel(Rb));
endmodule

module Vector2BR (
  input  [1:0] Ra,
  input  [1:0] Rb,
  input  CLK,
  input  [7:0] Data,
  input  WriteEnable,
  input  [1:0] WriteRegister,
  input  Reset,
  output [7:0] Rd1,
  output [7:0] Rd2
);

  wire W1, W2, W3;
  wire [7:0] R0, R1, R2, R3;

  Demultiplexer #(.select(2)) demultiplexer_1 (
    .out1(W1), .out2(W2), .out3(W3), .in(WriteEnable), .sel(WriteRegister));  // open: out0
  Register u_R0 (.D(8'h2), .en(Reset), .clk(Reset), .Q(R0), .clr(1'b0));
  Register u_R1 (.D(Data), .en(W1), .clk(CLK), .Q(R1), .clr(Reset));
  Register u_R2 (.D(Data), .en(W2), .clk(CLK), .Q(R2), .clr(Reset));
  Register u_R3 (.D(Data), .en(W3), .clk(CLK), .Q(R3), .clr(Reset));
  Multiplexer #(.select(2), .width(8)) multiplexer_1 (.in0(R0), .in1(R1), .in2(R2), .in3(R3), .out(Rd1), .sel(Ra));
  Multiplexer #(.select(2), .width(8)) multiplexer_2 (.in0(R0), .in1(R1), .in2(R2), .in3(R3), .out(Rd2), .sel(Rb));
endmodule

module Vector1BR (
  input  [1:0] Ra,
  input  [1:0] Rb,
  input  CLK,
  input  [7:0] Data,
  input  WriteEnable,
  input  [1:0] WriteRegister,
  input  Reset,
  output [7:0] Rd1,
  output [7:0] Rd2
);

  wire W1, W2, W3;
  wire [7:0] R0, R1, R2, R3;

  Demultiplexer #(.select(2)) demultiplexer_1 (
    .out1(W1), .out2(W2), .out3(W3), .in(WriteEnable), .sel(WriteRegister));  // open: out0
  Register u_R0 (.D(8'h1), .en(Reset), .clk(Reset), .Q(R0), .clr(1'b0));
  Register u_R1 (.D(Data), .en(W1), .clk(CLK), .Q(R1), .clr(Reset));
  Register u_R2 (.D(Data), .en(W2), .clk(CLK), .Q(R2), .clr(Reset));
  Register u_R3 (.D(Data), .en(W3), .clk(CLK), .Q(R3), .clr(Reset));
  Multiplexer #(.select(2), .width(8)) multiplexer_1 (.in0(R0), .in1(R1), .in2(R2), .in3(R3), .out(Rd1), .sel(Ra));
  Multiplexer #(.select(2), .width(8)) multiplexer_2 (.in0(R0), .in1(R1), .in2(R2), .in3(R3), .out(Rd2), .sel(Rb));
endmodule

module MOV_L (
  input  [7:0] R1,
  input  [3:0] IMM,
  output [7:0] S
);


  assign S = {R1[7:4], IMM};
endmodule

module MOV_H (
  input  [7:0] R1,
  input  [3:0] IMM,
  output [7:0] S
);


  assign S = {IMM, R1[3:0]};
endmodule

module Controle (
  input  [3:0] Opcode,
  output [1:0] Reg_Src_Vector,
  output V_RWE,
  output V_WE,
  output [1:0] V_ALU_Control,
  output V_Reg_D,
  output Branch,
  output [1:0] Reg_Src_Scalar,
  output S_RWE,
  output S_WE,
  output [1:0] S_ALU_Control,
  output S_Reg_D
);

  ROM #(.addrWidth(4), .dataWidth(15)) rom_1 (
    .addr(Opcode),
    .data({S_Reg_D, S_ALU_Control, S_WE, S_RWE, Reg_Src_Scalar, Branch, V_Reg_D, V_ALU_Control, V_WE, V_RWE, Reg_Src_Vector}));

  // Notes on the sheet:
  //   contents of rom_1 (hex, n*v repeats v):
  //   400 800 4700 4600 500 1500 2500 80 4 8 47 46 5 15 25 35
endmodule
