// Logisim project sagui.circ as structural Verilog: 15 circuits, main circuit main
module main (
);

  wire and_1_out, Branch, CLK, forwarding_1_p1, or_1_out, Reset, S_EX_MEM_s_m, S_EX_MEM_s_wb,
       S_ID_EX_s_branch, S_ID_EX_s_m, S_ID_EX_s_wb, S_MEM_WB_s_wb, S_Reg_D, S_RWE, S_WE, ScalarALU_zero,
       V_Reg_D, V_RWE, V_WE;
  wire [1:0] Decode_s_ra, Decode_s_rb, multiplexer_2_out, Reg_Src_Scalar, Reg_Src_Vector, S_ALU_Control,
       S_EX_MEM_s_reg_d, S_EX_MEM_s_reg_src, S_ID_EX_s_alu, S_ID_EX_s_r1, S_ID_EX_s_r2, S_ID_EX_s_reg_d,
       S_ID_EX_s_reg_src, S_MEM_WB_s_reg_d, S_MEM_WB_s_reg_src, V_ALU_Control, V_Ra, V_Rb, V_Rd;
  wire [3:0] Decode_imm, Decode_opcode, IMM;
  wire [7:0] adder_1_out, MOVH_S_s, MOVL_S_s, multiplexer_1_out, multiplexer_4_out, multiplexer_5_out,
       multiplexer_6_out, PC_q, ram_1_dout, ram_2_dout, ram_3_dout, ram_4_dout, ram_5_dout, rom_1_data,
       S_EX_MEM_s_movh, S_EX_MEM_s_movl, S_EX_MEM_s_rd1, S_EX_MEM_s_rd2, S_EX_MEM_s_s, S_ID_EX_s_movh,
       S_ID_EX_s_movl, S_ID_EX_s_rd1, S_ID_EX_s_rd2, S_IF_ID_s_ins, S_MEM_WB_s_m_data, S_MEM_WB_s_movh,
       S_MEM_WB_s_movl, S_MEM_WB_s_s, ScalarALU_s, ScalarBR_rd1, ScalarBR_rd2, V0_Data, V0_MOVH, V0_MOVL,
       V0_Rd1, V0_Rd2, V0_S, V1_Data, V1_MOVH, V1_MOVL, V1_Rd1, V1_Rd2, V1_S, V2_Data, V2_MOVH, V2_MOVL,
       V2_Rd1, V2_Rd2, V2_S, V3_Data, V3_MOVH, V3_MOVL, V3_Rd1, V3_Rd2, V3_S;

  Multiplexer #(.width(8)) multiplexer_1 (
    .in0(adder_1_out), .in1(S_EX_MEM_s_rd2), .out(multiplexer_1_out), .sel(and_1_out));
  Register PC (.D(multiplexer_1_out), .en(1'b1), .clk(CLK), .Q(PC_q), .clr(Reset));
  Clock clock_1 (.out(CLK));
  Button button_1 (.out(Reset));
  Adder adder_1 (.a(8'h1), .b(PC_q), .out(adder_1_out));  // open: cin, cout
  ROM rom_1 (.addr(PC_q), .data(rom_1_data));
  MOV_L MOVL_V0 (.R1(V0_Rd1), .IMM(IMM), .S(V0_MOVL));
  MOV_H MOVH_V0 (.R1(V0_Rd1), .IMM(IMM), .S(V0_MOVH));
  MOV_L MOVL_V1 (.R1(V1_Rd1), .IMM(IMM), .S(V1_MOVL));
  MOV_H MOVH_V1 (.R1(V1_Rd1), .IMM(IMM), .S(V1_MOVH));
  MOV_L MOVL_V2 (.R1(V2_Rd1), .IMM(IMM), .S(V2_MOVL));
  MOV_H MOVH_V2 (.R1(V2_Rd1), .IMM(IMM), .S(V2_MOVH));
  MOV_L MOVL_V3 (.R1(V3_Rd1), .IMM(IMM), .S(V3_MOVL));
  MOV_H MOVH_V3 (.R1(V3_Rd1), .IMM(IMM), .S(V3_MOVH));
  Controle Control_Center (
    .Opcode(Decode_opcode), .Reg_Src_Vector(Reg_Src_Vector), .V_RWE(V_RWE), .V_WE(V_WE),
    .V_ALU_Control(V_ALU_Control), .V_Reg_D(V_Reg_D), .Branch(Branch), .Reg_Src_Scalar(Reg_Src_Scalar),
    .S_RWE(S_RWE), .S_WE(S_WE), .S_ALU_Control(S_ALU_Control), .S_Reg_D(S_Reg_D));
  if_id S_IF_ID (.Ins(rom_1_data), .NOP(and_1_out), .CLK(CLK), .Reset(Reset), .S_Ins(S_IF_ID_s_ins));  // open: PC, S_PC
  Inst_Decoder Decode (
    .Data(S_IF_ID_s_ins), .V_Ra(V_Ra), .V_Rb(V_Rb), .S_Ra(Decode_s_ra), .S_Rb(Decode_s_rb), .IMM(Decode_imm),
    .Opcode(Decode_opcode));
  Multiplexer #(.width(2)) multiplexer_2 (.in0(Decode_s_ra), .in1(2'b01), .out(multiplexer_2_out), .sel(S_Reg_D));
  Multiplexer #(.width(2)) multiplexer_3 (.in0(V_Ra), .in1(2'b01), .out(V_Rd), .sel(V_Reg_D));
  Scalar_BR ScalarBR (
    .CLK(CLK), .WriteEnable(S_MEM_WB_s_wb), .Reset(Reset), .Ra(multiplexer_2_out), .Rb(Decode_s_rb),
    .WriteRegister(S_MEM_WB_s_reg_d), .Data(multiplexer_6_out), .Rd1(ScalarBR_rd1), .Rd2(ScalarBR_rd2));
  MOV_L MOVL_S (.R1(ScalarBR_rd1), .IMM(Decode_imm), .S(MOVL_S_s));
  MOV_H MOVH_S (.R1(ScalarBR_rd1), .IMM(Decode_imm), .S(MOVH_S_s));
  id_ex S_ID_EX (
    .NOP(and_1_out), .Reg_D(multiplexer_2_out), .MOVL(MOVL_S_s), .MOVH(MOVH_S_s), .Reg_Src(Reg_Src_Scalar),
    .R1(multiplexer_2_out), .R2(Decode_s_rb), .WB(S_RWE), .M(S_WE), .ALU(S_ALU_Control), .Branch(Branch),
    .RD1(ScalarBR_rd1), .RD2(ScalarBR_rd2), .CLK(CLK), .Reset(Reset), .S_Reg_D(S_ID_EX_s_reg_d),
    .S_MOVL(S_ID_EX_s_movl), .S_MOVH(S_ID_EX_s_movh), .S_Reg_Src(S_ID_EX_s_reg_src), .S_R1(S_ID_EX_s_r1),
    .S_R2(S_ID_EX_s_r2), .S_WB(S_ID_EX_s_wb), .S_M(S_ID_EX_s_m), .S_ALU(S_ID_EX_s_alu),
    .S_Branch(S_ID_EX_s_branch), .S_RD1(S_ID_EX_s_rd1), .S_RD2(S_ID_EX_s_rd2));  // open: PC, S_PC
  Multiplexer #(.width(8)) multiplexer_4 (
    .in0(S_ID_EX_s_rd1), .in1(S_EX_MEM_s_s), .out(multiplexer_4_out), .sel(forwarding_1_p1));
  Multiplexer #(.width(8)) multiplexer_5 (
    .in0(S_ID_EX_s_rd2), .in1(S_EX_MEM_s_s), .out(multiplexer_5_out), .sel(forwarding_1_p1));
  // Forwarding forwarding_1: pin names not known; wires that end beside it: forwarding_1_p1
  Scalar_BR VectorBR0 (
    .CLK(CLK), .WriteEnable(V_RWE), .Reset(Reset), .Ra(V_Rd), .Rb(V_Rb), .WriteRegister(V_Rd),
    .Data(V0_Data), .Rd1(V0_Rd1), .Rd2(V0_Rd2));
  Vector1BR VectorBR1 (
    .CLK(CLK), .WriteEnable(V_RWE), .Reset(Reset), .Ra(V_Rd), .Rb(V_Rb), .WriteRegister(V_Rd),
    .Data(V1_Data), .Rd1(V1_Rd1), .Rd2(V1_Rd2));
  Vector2BR VectorBR2 (
    .CLK(CLK), .WriteEnable(V_RWE), .Reset(Reset), .Ra(V_Rd), .Rb(V_Rb), .WriteRegister(V_Rd),
    .Data(V2_Data), .Rd1(V2_Rd1), .Rd2(V2_Rd2));
  Vector3BR VectorBR3 (
    .CLK(CLK), .WriteEnable(V_RWE), .Reset(Reset), .Ra(V_Rd), .Rb(V_Rb), .WriteRegister(V_Rd),
    .Data(V3_Data), .Rd1(V3_Rd1), .Rd2(V3_Rd2));
  and and_1 (and_1_out, S_ID_EX_s_branch, ScalarALU_zero);
  ULA ScalarALU (
    .RA(multiplexer_4_out), .RB(multiplexer_5_out), .ALU_Control(S_ID_EX_s_alu), .S(ScalarALU_s),
    .ZERO(ScalarALU_zero));
  ex_mem S_EX_MEM (
    .RD2(multiplexer_5_out), .Reg_D(S_ID_EX_s_reg_d), .MOVL(S_ID_EX_s_movl), .MOVH(S_ID_EX_s_movh),
    .Reg_Src(S_ID_EX_s_reg_src), .WB(S_ID_EX_s_wb), .M(S_ID_EX_s_m), .RD1(multiplexer_4_out),
    .S(ScalarALU_s), .CLK(CLK), .Reset(Reset), .S_RD2(S_EX_MEM_s_rd2), .S_Reg_D(S_EX_MEM_s_reg_d),
    .S_MOVL(S_EX_MEM_s_movl), .S_MOVH(S_EX_MEM_s_movh), .S_Reg_Src(S_EX_MEM_s_reg_src), .S_WB(S_EX_MEM_s_wb),
    .S_M(S_EX_MEM_s_m), .S_RD1(S_EX_MEM_s_rd1), .S_S(S_EX_MEM_s_s));  // open: PC, Branch, ZERO, S_PC, S_Branch, S_ZERO
  ULA VectorALU0 (.RA(V0_Rd1), .RB(V0_Rd2), .ALU_Control(V_ALU_Control), .S(V0_S));  // open: ZERO
  ULA VectorALU1 (.RA(V1_Rd1), .RB(V1_Rd2), .ALU_Control(V_ALU_Control), .S(V1_S));  // open: ZERO
  ULA VectorALU2 (.RA(V2_Rd1), .RB(V2_Rd2), .ALU_Control(V_ALU_Control), .S(V2_S));  // open: ZERO
  ULA VectorALU3 (.RA(V3_Rd1), .RB(V3_Rd2), .ALU_Control(V_ALU_Control), .S(V3_S));  // open: ZERO
  RAM #(.asyncread("true")) ram_1 (
    .addr(S_EX_MEM_s_rd2), .we(S_EX_MEM_s_m), .oe(1'b1), .clk(CLK), .din(S_EX_MEM_s_rd1), .dout(ram_1_dout));
  RAM #(.asyncread("true")) ram_2 (.addr(V0_Rd2), .we(V_WE), .oe(1'b1), .clk(CLK), .din(V0_Rd1), .dout(ram_2_dout));
  RAM #(.asyncread("true")) ram_3 (.addr(V1_Rd2), .we(V_WE), .oe(1'b1), .clk(CLK), .din(V1_Rd1), .dout(ram_3_dout));
  RAM #(.asyncread("true")) ram_4 (.addr(V2_Rd2), .we(V_WE), .oe(1'b1), .clk(CLK), .din(V2_Rd1), .dout(ram_4_dout));
  RAM #(.asyncread("true")) ram_5 (.addr(V3_Rd2), .we(V_WE), .oe(1'b1), .clk(CLK), .din(V3_Rd1), .dout(ram_5_dout));
  or or_1 (or_1_out, S_MEM_WB_s_wb, S_EX_MEM_s_wb);
  mem_wb S_MEM_WB (
    .Reg_Src(S_EX_MEM_s_reg_src), .MOVH(S_EX_MEM_s_movh), .Reg_D(S_EX_MEM_s_reg_d), .WB(S_EX_MEM_s_wb),
    .M_Data(ram_1_dout), .S(S_EX_MEM_s_s), .MOVL(S_EX_MEM_s_movl), .CLK(CLK), .Reset(Reset),
    .S_Reg_Src(S_MEM_WB_s_reg_src), .S_WB(S_MEM_WB_s_wb), .S_M_Data(S_MEM_WB_s_m_data), .S_S(S_MEM_WB_s_s),
    .S_MOVL(S_MEM_WB_s_movl), .S_MOVH(S_MEM_WB_s_movh), .S_Reg_D(S_MEM_WB_s_reg_d));
  Multiplexer #(.select(2), .width(8)) multiplexer_6 (
    .in0(S_MEM_WB_s_m_data), .in1(S_MEM_WB_s_s), .in2(S_MEM_WB_s_movl), .in3(S_MEM_WB_s_movh),
    .out(multiplexer_6_out), .sel(S_MEM_WB_s_reg_src));
  Multiplexer #(.select(2), .width(8)) multiplexer_7 (
    .in0(ram_2_dout), .in1(V0_S), .in2(V0_MOVL), .in3(V0_MOVH), .out(V0_Data), .sel(Reg_Src_Vector));
  Multiplexer #(.select(2), .width(8)) multiplexer_8 (
    .in0(ram_3_dout), .in1(V1_S), .in2(V1_MOVL), .in3(V1_MOVH), .out(V1_Data), .sel(Reg_Src_Vector));
  Multiplexer #(.select(2), .width(8)) multiplexer_9 (
    .in0(ram_4_dout), .in1(V2_S), .in2(V2_MOVL), .in3(V2_MOVH), .out(V2_Data), .sel(Reg_Src_Vector));
  Multiplexer #(.select(2), .width(8)) multiplexer_10 (
    .in0(ram_5_dout), .in1(V3_S), .in2(V3_MOVL), .in3(V3_MOVH), .out(V3_Data), .sel(Reg_Src_Vector));

  // Notes on the sheet:
  //   contents of rom_1 (hex, n*v repeats v):
  //   31 21 14 55 31 4d 33 22 17 55 33 b4 a1 c9 d5 cc c8 b 9f bc cd 9b cd b0 97 bc dd dd b4 cd c9 57 76 8
  //   72 3b 49 18 32 21 49 1b 55 33 df cc b 8b bc cd 87 c9 d5 bc cd 9b dd dd b4 cd 57 76 8 72 72
endmodule

module Scalar_BR (
  input  [1:0] Ra,
  input  [1:0] Rb,
  input  CLK,
  input  [7:0] Data,
  input  WriteEnable,
  input  [1:0] WriteRegister,
  input  Reset,
  output [7:0] Rd1,
  output [7:0] Rd2
);

  wire W1, W2, W3;
  wire [7:0] R0, R1, R2, R3;

  Demultiplexer #(.select(2)) demultiplexer_1 (
    .out1(W1), .out2(W2), .out3(W3), .in(WriteEnable), .sel(WriteRegister));  // open: out0
  Register u_R0 (.D({8{1'b0}}), .en(Reset), .clk(Reset), .Q(R0), .clr(1'b0));
  Register u_R1 (.D(Data), .en(W1), .clk(CLK), .Q(R1), .clr(Reset));
  Register u_R2 (.D(Data), .en(W2), .clk(CLK), .Q(R2), .clr(Reset));
  Register u_R3 (.D(Data), .en(W3), .clk(CLK), .Q(R3), .clr(Reset));
  Multiplexer #(.select(2), .width(8)) multiplexer_1 (.in0(R0), .in1(R1), .in2(R2), .in3(R3), .out(Rd1), .sel(Ra));
  Multiplexer #(.select(2), .width(8)) multiplexer_2 (.in0(R0), .in1(R1), .in2(R2), .in3(R3), .out(Rd2), .sel(Rb));
endmodule

module ULA (
  input  [7:0] RA,
  input  [7:0] RB,
  input  [1:0] ALU_Control,
  output ZERO,
  output [7:0] S
);

  wire [7:0] adder_1_out, and_1_out, not_1_out, or_1_out, subtractor_1_out;

  assign not_1_out = ~RA;  // NOT_Gate not_1, 8 bits wide
  Adder adder_1 (.a(RA), .b(RB), .out(adder_1_out));  // open: cin, cout
  Subtractor subtractor_1 (.a(RA), .b(RB), .out(subtractor_1_out));  // open: bin, bout
  assign and_1_out = RA & RB;  // AND_Gate and_1, 8 bits wide
  assign or_1_out = RA | RB;  // OR_Gate or_1, 8 bits wide
  and and_2 (ZERO, not_1_out[0], not_1_out[1], not_1_out[2], not_1_out[3], not_1_out[4], not_1_out[5], not_1_out[6], not_1_out[7]);
  Multiplexer #(.select(2), .width(8)) multiplexer_1 (
    .in0(adder_1_out), .in1(subtractor_1_out), .in2(and_1_out), .in3(or_1_out), .out(S), .sel(ALU_Control));
endmodule

module Inst_Decoder (
  input  [7:0] Data,
  output [1:0] V_Ra,
  output [1:0] V_Rb,
  output [1:0] S_Ra,
  output [1:0] S_Rb,
  output [3:0] IMM,
  output [3:0] Opcode
);

  Demultiplexer #(.width(4)) demultiplexer_1 (.out0({S_Ra, S_Rb}), .out1({V_Ra, V_Rb}), .in(Data[3:0]), .sel(Data[7]));

  assign IMM = Data[3:0];
  assign Opcode = Data[7:4];

  // Other names for the same wires on the sheet: Rb[1:0] = V_Rb; Ra[1:0] = V_Ra
endmodule

module Vector3BR (
  input  [1:0] Ra,
  input  [1:0] Rb,
  input  CLK,
  input  [7:0] Data,
  input  WriteEnable,
  input  [1:0] WriteRegister,
  input  Reset,
  output [7:0] Rd1,
  output [7:0] Rd2
);

  wire W1, W2, W3;
  wire [7:0] R0, R1, R2, R3;

  Demultiplexer #(.select(2)) demultiplexer_1 (
    .out1(W1), .out2(W2), .out3(W3), .in(WriteEnable), .sel(WriteRegister));  // open: out0
  Register u_R0 (.D(8'h3), .en(Reset), .clk(Reset), .Q(R0), .clr(1'b0));
  Register u_R1 (.D(Data), .en(W1), .clk(CLK), .Q(R1), .clr(Reset));
  Register u_R2 (.D(Data), .en(W2), .clk(CLK), .Q(R2), .clr(Reset));
  Register u_R3 (.D(Data), .en(W3), .clk(CLK), .Q(R3), .clr(Reset));
  Multiplexer #(.select(2), .width(8)) multiplexer_1 (.in0(R0), .in1(R1), .in2(R2), .in3(R3), .out(Rd1), .sel(Ra));
  Multiplexer #(.select(2), .width(8)) multiplexer_2 (.in0(R0), .in1(R1), .in2(R2), .in3(R3), .out(Rd2), .sel(Rb));
endmodule

module Vector2BR (
  input  [1:0] Ra,
  input  [1:0] Rb,
  input  CLK,
  input  [7:0] Data,
  input  WriteEnable,
  input  [1:0] WriteRegister,
  input  Reset,
  output [7:0] Rd1,
  output [7:0] Rd2
);

  wire W1, W2, W3;
  wire [7:0] R0, R1, R2, R3;

  Demultiplexer #(.select(2)) demultiplexer_1 (
    .out1(W1), .out2(W2), .out3(W3), .in(WriteEnable), .sel(WriteRegister));  // open: out0
  Register u_R0 (.D(8'h2), .en(Reset), .clk(Reset), .Q(R0), .clr(1'b0));
  Register u_R1 (.D(Data), .en(W1), .clk(CLK), .Q(R1), .clr(Reset));
  Register u_R2 (.D(Data), .en(W2), .clk(CLK), .Q(R2), .clr(Reset));
  Register u_R3 (.D(Data), .en(W3), .clk(CLK), .Q(R3), .clr(Reset));
  Multiplexer #(.select(2), .width(8)) multiplexer_1 (.in0(R0), .in1(R1), .in2(R2), .in3(R3), .out(Rd1), .sel(Ra));
  Multiplexer #(.select(2), .width(8)) multiplexer_2 (.in0(R0), .in1(R1), .in2(R2), .in3(R3), .out(Rd2), .sel(Rb));
endmodule

module Vector1BR (
  input  [1:0] Ra,
  input  [1:0] Rb,
  input  CLK,
  input  [7:0] Data,
  input  WriteEnable,
  input  [1:0] WriteRegister,
  input  Reset,
  output [7:0] Rd1,
  output [7:0] Rd2
);

  wire W1, W2, W3;
  wire [7:0] R0, R1, R2, R3;

  Demultiplexer #(.select(2)) demultiplexer_1 (
    .out1(W1), .out2(W2), .out3(W3), .in(WriteEnable), .sel(WriteRegister));  // open: out0
  Register u_R0 (.D(8'h1), .en(Reset), .clk(Reset), .Q(R0), .clr(1'b0));
  Register u_R1 (.D(Data), .en(W1), .clk(CLK), .Q(R1), .clr(Reset));
  Register u_R2 (.D(Data), .en(W2), .clk(CLK), .Q(R2), .clr(Reset));
  Register u_R3 (.D(Data), .en(W3), .clk(CLK), .Q(R3), .clr(Reset));
  Multiplexer #(.select(2), .width(8)) multiplexer_1 (.in0(R0), .in1(R1), .in2(R2), .in3(R3), .out(Rd1), .sel(Ra));
  Multiplexer #(.select(2), .width(8)) multiplexer_2 (.in0(R0), .in1(R1), .in2(R2), .in3(R3), .out(Rd2), .sel(Rb));
endmodule

module MOV_L (
  input  [7:0] R1,
  input  [3:0] IMM,
  output [7:0] S
);


  assign S = {R1[7:4], IMM};
endmodule

module MOV_H (
  input  [7:0] R1,
  input  [3:0] IMM,
  output [7:0] S
);


  assign S = {IMM, R1[3:0]};
endmodule

module Controle (
  input  [3:0] Opcode,
  output [1:0] Reg_Src_Vector,
  output V_RWE,
  output V_WE,
  output [1:0] V_ALU_Control,
  output V_Reg_D,
  output Branch,
  output [1:0] Reg_Src_Scalar,
  output S_RWE,
  output S_WE,
  output [1:0] S_ALU_Control,
  output S_Reg_D
);

  ROM #(.addrWidth(4), .dataWidth(15)) rom_1 (
    .addr(Opcode),
    .data({S_Reg_D, S_ALU_Control, S_WE, S_RWE, Reg_Src_Scalar, Branch, V_Reg_D, V_ALU_Control, V_WE, V_RWE, Reg_Src_Vector}));

  // Notes on the sheet:
  //   contents of rom_1 (hex, n*v repeats v):
  //   400 800 4700 4600 500 1500 2500 80 4 8 47 46 5 15 25 35
endmodule

module if_id (
  input  CLK,
  input  Reset,
  input  [7:0] PC,
  input  [7:0] Ins,
  input  NOP,
  output [7:0] S_PC,
  output [7:0] S_Ins
);

  wire [7:0] multiplexer_1_out, multiplexer_2_out, register_1_q, register_2_q;

  Multiplexer #(.width(8)) multiplexer_1 (.in0(PC), .in1({8{1'b0}}), .out(multiplexer_1_out), .sel(NOP));
  Multiplexer #(.width(8)) multiplexer_2 (.in0(Ins), .in1({8{1'b0}}), .out(multiplexer_2_out), .sel(NOP));
  Register register_1 (.D(multiplexer_1_out), .en(1'b1), .clk(CLK), .Q(register_1_q), .clr(Reset));
  Register register_2 (.D(multiplexer_2_out), .en(1'b1), .clk(CLK), .Q(register_2_q), .clr(Reset));
  Register #(.trigger("falling")) register_3 (.D(register_1_q), .en(1'b1), .clk(CLK), .Q(S_PC), .clr(Reset));
  Register #(.trigger("falling")) register_4 (.D(register_2_q), .en(1'b1), .clk(CLK), .Q(S_Ins), .clr(Reset));
endmodule

module id_ex (
  input  CLK,
  input  Reset,
  input  [7:0] PC,
  input  WB,
  input  M,
  input  [1:0] ALU,
  input  Branch,
  input  [7:0] RD1,
  input  [7:0] RD2,
  input  [1:0] Reg_D,
  input  [7:0] MOVL,
  input  [7:0] MOVH,
  input  [1:0] Reg_Src,
  input  [1:0] R1,
  input  [1:0] R2,
  input  NOP,
  output [7:0] S_PC,
  output S_WB,
  output S_M,
  output [1:0] S_ALU,
  output S_Branch,
  output [7:0] S_RD1,
  output [7:0] S_RD2,
  output [1:0] S_Reg_D,
  output [7:0] S_MOVL,
  output [7:0] S_MOVH,
  output [1:0] S_Reg_Src,
  output [1:0] S_R1,
  output [1:0] S_R2
);

  wire multiplexer_2_out, multiplexer_3_out, multiplexer_5_out, register_2_q, register_3_q, register_5_q;
  wire [1:0] multiplexer_4_out, multiplexer_8_out, multiplexer_11_out, multiplexer_12_out,
       multiplexer_13_out, register_4_q, register_8_q, register_11_q, register_12_q, register_13_q;
  wire [7:0] multiplexer_1_out, multiplexer_6_out, multiplexer_7_out, multiplexer_9_out, multiplexer_10_out,
       register_1_q, register_6_q, register_7_q, register_9_q, register_10_q;

  Multiplexer #(.width(8)) multiplexer_1 (.in0(PC), .in1({8{1'b0}}), .out(multiplexer_1_out), .sel(NOP));
  Multiplexer multiplexer_2 (.in0(WB), .in1(1'b0), .out(multiplexer_2_out), .sel(NOP));
  Multiplexer multiplexer_3 (.in0(M), .in1(1'b0), .out(multiplexer_3_out), .sel(NOP));
  Multiplexer #(.width(2)) multiplexer_4 (.in0(ALU), .in1(2'b00), .out(multiplexer_4_out), .sel(NOP));
  Multiplexer multiplexer_5 (.in0(Branch), .in1(1'b0), .out(multiplexer_5_out), .sel(NOP));
  Multiplexer #(.width(8)) multiplexer_6 (.in0(RD1), .in1({8{1'b0}}), .out(multiplexer_6_out), .sel(NOP));
  Multiplexer #(.width(8)) multiplexer_7 (.in0(RD2), .in1({8{1'b0}}), .out(multiplexer_7_out), .sel(NOP));
  Multiplexer #(.width(2)) multiplexer_8 (.in0(Reg_D), .in1(2'b00), .out(multiplexer_8_out), .sel(NOP));
  Multiplexer #(.width(8)) multiplexer_9 (.in0(MOVL), .in1({8{1'b0}}), .out(multiplexer_9_out), .sel(NOP));
  Multiplexer #(.width(8)) multiplexer_10 (.in0(MOVH), .in1({8{1'b0}}), .out(multiplexer_10_out), .sel(NOP));
  Multiplexer #(.width(2)) multiplexer_11 (.in0(Reg_Src), .in1(2'b00), .out(multiplexer_11_out), .sel(NOP));
  Multiplexer #(.width(2)) multiplexer_12 (.in0(R1), .in1(2'b00), .out(multiplexer_12_out), .sel(NOP));
  Multiplexer #(.width(2)) multiplexer_13 (.in0(R2), .in1(2'b00), .out(multiplexer_13_out), .sel(NOP));
  Register register_1 (.D(multiplexer_1_out), .en(1'b1), .clk(CLK), .Q(register_1_q), .clr(Reset));
  Register #(.width(1)) register_2 (.D(multiplexer_2_out), .en(1'b1), .clk(CLK), .Q(register_2_q), .clr(Reset));
  Register #(.width(1)) register_3 (.D(multiplexer_3_out), .en(1'b1), .clk(CLK), .Q(register_3_q), .clr(Reset));
  Register #(.width(2)) register_4 (.D(multiplexer_4_out), .en(1'b1), .clk(CLK), .Q(register_4_q), .clr(Reset));
  Register #(.width(1)) register_5 (.D(multiplexer_5_out), .en(1'b1), .clk(CLK), .Q(register_5_q), .clr(Reset));
  Register register_6 (.D(multiplexer_6_out), .en(1'b1), .clk(CLK), .Q(register_6_q), .clr(Reset));
  Register register_7 (.D(multiplexer_7_out), .en(1'b1), .clk(CLK), .Q(register_7_q), .clr(Reset));
  Register #(.width(2)) register_8 (.D(multiplexer_8_out), .en(1'b1), .clk(CLK), .Q(register_8_q), .clr(Reset));
  Register register_9 (.D(multiplexer_9_out), .en(1'b1), .clk(CLK), .Q(register_9_q), .clr(Reset));
  Register register_10 (.D(multiplexer_10_out), .en(1'b1), .clk(CLK), .Q(register_10_q), .clr(Reset));
  Register #(.width(2)) register_11 (.D(multiplexer_11_out), .en(1'b1), .clk(CLK), .Q(register_11_q), .clr(Reset));
  Register #(.width(2)) register_12 (.D(multiplexer_12_out), .en(1'b1), .clk(CLK), .Q(register_12_q), .clr(Reset));
  Register #(.width(2)) register_13 (.D(multiplexer_13_out), .en(1'b1), .clk(CLK), .Q(register_13_q), .clr(Reset));
  Register register_14 (.D(register_1_q), .en(1'b1), .clk(CLK), .Q(S_PC), .clr(Reset));
  Register #(.trigger("falling"), .width(1)) register_15 (
    .D(register_2_q), .en(1'b1), .clk(CLK), .Q(S_WB), .clr(Reset));
  Register #(.trigger("falling"), .width(1)) register_16 (.D(register_3_q), .en(1'b1), .clk(CLK), .Q(S_M), .clr(Reset));
  Register #(.trigger("falling"), .width(2)) register_17 (
    .D(register_4_q), .en(1'b1), .clk(CLK), .Q(S_ALU), .clr(Reset));
  Register #(.trigger("falling"), .width(1)) register_18 (
    .D(register_5_q), .en(1'b1), .clk(CLK), .Q(S_Branch), .clr(Reset));
  Register #(.trigger("falling")) register_19 (.D(register_6_q), .en(1'b1), .clk(CLK), .Q(S_RD1), .clr(Reset));
  Register #(.trigger("falling")) register_20 (.D(register_7_q), .en(1'b1), .clk(CLK), .Q(S_RD2), .clr(Reset));
  Register #(.trigger("falling"), .width(2)) register_21 (
    .D(register_8_q), .en(1'b1), .clk(CLK), .Q(S_Reg_D), .clr(Reset));
  Register #(.trigger("falling")) register_22 (.D(register_9_q), .en(1'b1), .clk(CLK), .Q(S_MOVL), .clr(Reset));
  Register #(.trigger("falling")) register_23 (.D(register_10_q), .en(1'b1), .clk(CLK), .Q(S_MOVH), .clr(Reset));
  Register #(.trigger("falling"), .width(2)) register_24 (
    .D(register_11_q), .en(1'b1), .clk(CLK), .Q(S_Reg_Src), .clr(Reset));
  Register #(.trigger("falling"), .width(2)) register_25 (
    .D(register_12_q), .en(1'b1), .clk(CLK), .Q(S_R1), .clr(Reset));
  Register #(.trigger("falling"), .width(2)) register_26 (
    .D(register_13_q), .en(1'b1), .clk(CLK), .Q(S_R2), .clr(Reset));
endmodule

module ex_mem (
  input  CLK,
  input  Reset,
  input  [7:0] PC,
  input  WB,
  input  M,
  input  [7:0] RD1,
  input  Branch,
  input  ZERO,
  input  [7:0] S,
  input  [7:0] RD2,
  input  [1:0] Reg_D,
  input  [7:0] MOVL,
  input  [7:0] MOVH,
  input  [1:0] Reg_Src,
  output [7:0] S_PC,
  output S_WB,
  output S_M,
  output [7:0] S_RD1,
  output S_Branch,
  output S_ZERO,
  output [7:0] S_S,
  output [7:0] S_RD2,
  output [1:0] S_Reg_D,
  output [7:0] S_MOVL,
  output [7:0] S_MOVH,
  output [1:0] S_Reg_Src
);

  wire register_2_q, register_3_q, register_5_q, register_6_q;
  wire [1:0] register_9_q, register_12_q;
  wire [7:0] register_1_q, register_4_q, register_7_q, register_8_q, register_10_q, register_11_q;

  Register register_1 (.D(PC), .en(1'b1), .clk(CLK), .Q(register_1_q), .clr(Reset));
  Register #(.width(1)) register_2 (.D(WB), .en(1'b1), .clk(CLK), .Q(register_2_q), .clr(Reset));
  Register #(.width(1)) register_3 (.D(M), .en(1'b1), .clk(CLK), .Q(register_3_q), .clr(Reset));
  Register register_4 (.D(RD1), .en(1'b1), .clk(CLK), .Q(register_4_q), .clr(Reset));
  Register #(.width(1)) register_5 (.D(Branch), .en(1'b1), .clk(CLK), .Q(register_5_q), .clr(Reset));
  Register #(.width(1)) register_6 (.D(ZERO), .en(1'b1), .clk(CLK), .Q(register_6_q), .clr(Reset));
  Register register_7 (.D(S), .en(1'b1), .clk(CLK), .Q(register_7_q), .clr(Reset));
  Register register_8 (.D(RD2), .en(1'b1), .clk(CLK), .Q(register_8_q), .clr(Reset));
  Register #(.width(2)) register_9 (.D(Reg_D), .en(1'b1), .clk(CLK), .Q(register_9_q), .clr(Reset));
  Register register_10 (.D(MOVL), .en(1'b1), .clk(CLK), .Q(register_10_q), .clr(Reset));
  Register register_11 (.D(MOVH), .en(1'b1), .clk(CLK), .Q(register_11_q), .clr(Reset));
  Register #(.width(2)) register_12 (.D(Reg_Src), .en(1'b1), .clk(CLK), .Q(register_12_q), .clr(Reset));
  Register register_13 (.D(register_1_q), .en(1'b1), .clk(CLK), .Q(S_PC), .clr(Reset));
  Register #(.trigger("falling"), .width(1)) register_14 (
    .D(register_2_q), .en(1'b1), .clk(CLK), .Q(S_WB), .clr(Reset));
  Register #(.trigger("falling"), .width(1)) register_15 (.D(register_3_q), .en(1'b1), .clk(CLK), .Q(S_M), .clr(Reset));
  Register #(.trigger("falling")) register_16 (.D(register_4_q), .en(1'b1), .clk(CLK), .Q(S_RD1), .clr(Reset));
  Register #(.trigger("falling"), .width(1)) register_17 (
    .D(register_5_q), .en(1'b1), .clk(CLK), .Q(S_Branch), .clr(Reset));
  Register #(.trigger("falling"), .width(1)) register_18 (
    .D(register_6_q), .en(1'b1), .clk(CLK), .Q(S_ZERO), .clr(Reset));
  Register #(.trigger("falling")) register_19 (.D(register_7_q), .en(1'b1), .clk(CLK), .Q(S_S), .clr(Reset));
  Register #(.trigger("falling")) register_20 (.D(register_8_q), .en(1'b1), .clk(CLK), .Q(S_RD2), .clr(Reset));
  Register #(.trigger("falling"), .width(2)) register_21 (
    .D(register_9_q), .en(1'b1), .clk(CLK), .Q(S_Reg_D), .clr(Reset));
  Register #(.trigger("falling")) register_22 (.D(register_10_q), .en(1'b1), .clk(CLK), .Q(S_MOVL), .clr(Reset));
  Register #(.trigger("falling")) register_23 (.D(register_11_q), .en(1'b1), .clk(CLK), .Q(S_MOVH), .clr(Reset));
  Register #(.trigger("falling"), .width(2)) register_24 (
    .D(register_12_q), .en(1'b1), .clk(CLK), .Q(S_Reg_Src), .clr(Reset));
endmodule

module mem_wb (
  input  CLK,
  input  Reset,
  input  WB,
  input  [7:0] M_Data,
  input  [7:0] S,
  input  [7:0] MOVL,
  input  [7:0] MOVH,
  input  [1:0] Reg_D,
  input  [1:0] Reg_Src,
  output S_WB,
  output [7:0] S_M_Data,
  output [7:0] S_S,
  output [7:0] S_MOVL,
  output [7:0] S_MOVH,
  output [1:0] S_Reg_D,
  output [1:0] S_Reg_Src
);

  wire register_1_q;
  wire [1:0] register_6_q, register_7_q;
  wire [7:0] register_2_q, register_3_q, register_4_q, register_5_q;

  Register #(.width(1)) register_1 (.D(WB), .en(1'b1), .clk(CLK), .Q(register_1_q), .clr(Reset));
  Register register_2 (.D(M_Data), .en(1'b1), .clk(CLK), .Q(register_2_q), .clr(Reset));
  Register register_3 (.D(S), .en(1'b1), .clk(CLK), .Q(register_3_q), .clr(Reset));
  Register register_4 (.D(MOVL), .en(1'b1), .clk(CLK), .Q(register_4_q), .clr(Reset));
  Register register_5 (.D(MOVH), .en(1'b1), .clk(CLK), .Q(register_5_q), .clr(Reset));
  Register #(.width(2)) register_6 (.D(Reg_D), .en(1'b1), .clk(CLK), .Q(register_6_q), .clr(Reset));
  Register #(.width(2)) register_7 (.D(Reg_Src), .en(1'b1), .clk(CLK), .Q(register_7_q), .clr(Reset));
  Register #(.trigger("falling"), .width(1)) register_8 (.D(register_1_q), .en(1'b1), .clk(CLK), .Q(S_WB), .clr(Reset));
  Register #(.trigger("falling")) register_9 (.D(register_2_q), .en(1'b1), .clk(CLK), .Q(S_M_Data), .clr(Reset));
  Register #(.trigger("falling")) register_10 (.D(register_3_q), .en(1'b1), .clk(CLK), .Q(S_S), .clr(Reset));
  Register #(.trigger("falling")) register_11 (.D(register_4_q), .en(1'b1), .clk(CLK), .Q(S_MOVL), .clr(Reset));
  Register #(.trigger("falling")) register_12 (.D(register_5_q), .en(1'b1), .clk(CLK), .Q(S_MOVH), .clr(Reset));
  Register #(.trigger("falling"), .width(2)) register_13 (
    .D(register_6_q), .en(1'b1), .clk(CLK), .Q(S_Reg_D), .clr(Reset));
  Register #(.trigger("falling"), .width(2)) register_14 (
    .D(register_7_q), .en(1'b1), .clk(CLK), .Q(S_Reg_Src), .clr(Reset));
endmodule

module Forwarding (
  input  [1:0] Reg_1,
  input  [1:0] Reg_Dest,
  input  [1:0] Reg_2,
  input  W_E,
  output S
);

  wire comparator_1_eq, comparator_2_eq, or_1_out;

  Comparator #(.width(2)) comparator_1 (.a(Reg_1), .b(Reg_Dest), .eq(comparator_1_eq));  // open: gt, lt
  Comparator #(.width(2)) comparator_2 (.a(Reg_Dest), .b(Reg_2), .eq(comparator_2_eq));  // open: gt, lt
  or or_1 (or_1_out, comparator_1_eq, comparator_2_eq);
  and and_1 (S, or_1_out, W_E);
endmodule
